// Logisim project 8-bit-CPU-logisim.circ as structural Verilog: 3 circuits, main circuit main
module main (
  input  [2:0] in_1,
  output out_2,
  output out_3,
  output out_4
);

  wire clock_1_out, cu_8bits_1_halt, cu_8bits_1_pc_inc, cu_8bits_1_regloadr0, cu_8bits_1_regloadr1;
  wire [1:0] cu_8bits_1_bussrc;
  wire [7:0] adder_1_out, alu_8bit_8ops_1_aluout_7_0, multiplexer_1_out, PC__8_bit_register_q, R0_q, R1_q,
       rom_1_data;
  wire [7:4] Instruction_Register__IR_q, Instruction_Register__IR_q_2;

  Clock clock_1 (.out(clock_1_out));
  Register PC__8_bit_register (
    .D(adder_1_out), .en(cu_8bits_1_pc_inc), .Q(PC__8_bit_register_q), .clk(clock_1_out));  // open: clr
  Adder adder_1 (.a(PC__8_bit_register_q), .b(8'h1), .out(adder_1_out));  // open: cin, cout
  Hex_Digit_Display hex_digit_display_1 (.value(PC__8_bit_register_q[7:4]));  // open: dp
  Hex_Digit_Display hex_digit_display_2 (.value(PC__8_bit_register_q[3:0]));  // open: dp
  ROM rom_1 (.addr(PC__8_bit_register_q), .data(rom_1_data));  // open: sel
  Register Instruction_Register__IR (
    .D(rom_1_data), .Q({Instruction_Register__IR_q, Instruction_Register__IR_q_2}), .clk(clock_1_out));  // open: en, clr
  Register R0 (.D(multiplexer_1_out), .en(cu_8bits_1_regloadr0), .Q(R0_q), .clk(clock_1_out));  // open: clr
  Register R1 (.D(multiplexer_1_out), .en(cu_8bits_1_regloadr1), .Q(R1_q), .clk(clock_1_out));  // open: clr
  Hex_Digit_Display hex_digit_display_3 (.value(Instruction_Register__IR_q));  // open: dp
  Hex_Digit_Display hex_digit_display_4 (.value(Instruction_Register__IR_q_2));  // open: dp
  Hex_Digit_Display hex_digit_display_5 (.value(R0_q[3:0]));  // open: dp
  Hex_Digit_Display hex_digit_display_6 (.value(R0_q[7:4]));  // open: dp
  Hex_Digit_Display hex_digit_display_7 (.value(R1_q[3:0]));  // open: dp
  Hex_Digit_Display hex_digit_display_8 (.value(R1_q[7:4]));  // open: dp
  Multiplexer #(.select(2), .width(8)) multiplexer_1 (
    .in0(alu_8bit_8ops_1_aluout_7_0), .in1({Instruction_Register__IR_q_2, 4'b0000}), .in2({8{1'b0}}),
    .in3({8{1'b0}}), .out(multiplexer_1_out), .sel(cu_8bits_1_bussrc));  // open: en
  CU_8bits cu_8bits_1 (
    .opcode_3_0(Instruction_Register__IR_q), .RegLoadR0(cu_8bits_1_regloadr0),
    .RegLoadR1(cu_8bits_1_regloadr1), .PC_Inc(cu_8bits_1_pc_inc), .BusSrc(cu_8bits_1_bussrc),
    .ALUop_2_0(in_1), .Halt(cu_8bits_1_halt));
  LED led_1 (.in(cu_8bits_1_halt));
  Hex_Digit_Display hex_digit_display_9 (.value(alu_8bit_8ops_1_aluout_7_0[3:0]));  // open: dp
  Hex_Digit_Display hex_digit_display_10 (.value(alu_8bit_8ops_1_aluout_7_0[7:4]));  // open: dp
  ALU_8bit_8ops alu_8bit_8ops_1 (
    .ALUop_2_0(in_1), .A_7_0(R1_q), .B_7_0(R0_q), .carry_flag(out_3),
    .ALUout_7_0(alu_8bit_8ops_1_aluout_7_0), .Zero(out_2), .Negative_Flag(out_4));  // open: in_3, in_4

  // Notes on the sheet:
  //   clock
  //   8 bit adder (+1)
  //   ROM
  //   contents of rom_1 (hex, n*v repeats v):
  //   1a 25 30 23 40 1f 26 50 21 30 70 80 1a 90 a0 f0
endmodule

// ALU
module ALU_8bit_8ops (
  input  [7:0] A_7_0,
  input  [7:0] B_7_0,
  input  [2:0] in_3,
  input  [2:0] in_4,
  input  [2:0] ALUop_2_0,
  output carry_flag,
  output [7:0] ALUout_7_0,
  output Zero,
  output Negative_Flag
);

  wire adder_1_cout, adder_2_cout, or_2_out, or_3_out, or_4_out, or_5_out, or_6_out, or_7_out;
  wire [7:0] adder_1_out, adder_2_out, and_1_out, nand_1_out, not_1_out, or_1_out, shifter_1_out,
       shifter_2_out, xor_1_out;

  assign not_1_out = ~B_7_0;  // NOT_Gate not_1, 8 bits wide
  Adder adder_1 (.a(A_7_0), .b(B_7_0), .out(adder_1_out), .cout(adder_1_cout));  // open: cin
  Adder adder_2 (.a(A_7_0), .b(not_1_out), .out(adder_2_out), .cin(1'b1), .cout(adder_2_cout));
  assign and_1_out = A_7_0 & B_7_0;  // AND_Gate and_1, 8 bits wide
  assign or_1_out = A_7_0 | B_7_0;  // OR_Gate or_1, 8 bits wide
  assign xor_1_out = A_7_0 ^ B_7_0;  // XOR_Gate xor_1, 8 bits wide
  assign nand_1_out = ~(A_7_0 & B_7_0);  // NAND_Gate nand_1, 8 bits wide
  Shifter shifter_1 (.in(A_7_0), .\dist (in_3), .out(shifter_1_out));
  Shifter #(.shift("lr")) shifter_2 (.in(A_7_0), .\dist (in_4), .out(shifter_2_out));
  Multiplexer #(.select(3)) multiplexer_1 (
    .in0(adder_1_cout), .in1(adder_2_cout), .in2(1'b0), .in3(1'b0), .in4(1'b0), .in5(1'b0), .in6(1'b0),
    .in7(1'b0), .out(carry_flag), .sel(ALUop_2_0));  // open: en
  Multiplexer #(.select(3), .width(8)) multiplexer_2 (
    .in0(adder_1_out), .in1(adder_2_out), .in2(and_1_out), .in3(or_1_out), .in4(xor_1_out), .in5(nand_1_out),
    .in6(shifter_1_out), .in7(shifter_2_out), .out(ALUout_7_0), .sel(ALUop_2_0));  // open: en
  or or_2 (or_2_out, ALUout_7_0[7], ALUout_7_0[6]);
  or or_3 (or_3_out, or_2_out, or_4_out);
  or or_4 (or_4_out, ALUout_7_0[5], ALUout_7_0[4]);
  or or_5 (or_5_out, ALUout_7_0[3], ALUout_7_0[2]);
  or or_6 (or_6_out, or_5_out, or_7_out);
  or or_7 (or_7_out, ALUout_7_0[1], ALUout_7_0[0]);
  or or_8 (Zero, or_3_out, or_6_out);

  assign Negative_Flag = ALUout_7_0[7];
endmodule

// CU
module CU_8bits (
  input  [3:0] opcode_3_0,
  output RegLoadR0,
  output RegLoadR1,
  output PC_Inc,
  output [1:0] BusSrc,
  output [2:0] ALUop_2_0,
  output Halt
);

  wire decoder_1_out1, decoder_1_out3, decoder_1_out4, decoder_1_out5, decoder_1_out6, decoder_1_out7,
       decoder_1_out8, decoder_1_out9, decoder_1_out10;

  Decoder #(.select(4)) decoder_1 (
    .out1(decoder_1_out1), .out2(RegLoadR1), .out3(decoder_1_out3), .out4(decoder_1_out4),
    .out5(decoder_1_out5), .out6(decoder_1_out6), .out7(decoder_1_out7), .out8(decoder_1_out8),
    .out9(decoder_1_out9), .out10(decoder_1_out10), .out15(Halt), .sel(opcode_3_0));  // open: out0, out11, out12, out13, out14, en
  or or_1 (RegLoadR0, decoder_1_out1, decoder_1_out10, decoder_1_out9, decoder_1_out8, decoder_1_out7, decoder_1_out6, decoder_1_out5, decoder_1_out4, decoder_1_out3);
  not not_1 (PC_Inc, Halt);
  or or_2 (BusSrc[0], RegLoadR1, decoder_1_out1);
  or or_3 (ALUop_2_0[2], decoder_1_out10, decoder_1_out9, decoder_1_out8, decoder_1_out7);
  or or_4 (ALUop_2_0[1], decoder_1_out10, decoder_1_out9, decoder_1_out6, decoder_1_out5);
  or or_5 (ALUop_2_0[0], decoder_1_out10, decoder_1_out8, decoder_1_out6, decoder_1_out4);

  assign BusSrc[1] = 1'b0;
endmodule
